# Fritzing sketch pcb (saved by Fritzing 0.9.3b)
circuit board: 13.0216cm x 19.0376cm
breadboards: 1

parts:
  Part1 = Arduino Mega 2560 (Rev3)
  U2 = RJ45 Jack [package=rj45-8]
  U3 = RJ45 Jack [package=rj45-8]
  U4 = RJ45 Jack [package=rj45-8]
  U5 = RJ45 Jack [package=rj45-8]
  U6 = RJ45 Jack [package=rj45-8]
  U7 = RJ45 Jack [package=rj45-8]
  J2 = female pin header, 2 pins [form="♀ (female)"]
  J3 = female pin header, 2 pins [form="♀ (female)"]
  U8 = ESP8266 NodeMCU LoLin module
  J7 = female pin header, 4 pins [form="♀ (female)"]
  LED1 = LED - 5mm [color="Red (633nm)" package="5 mm [THT]"]
  LED2 = LED - 5mm [color="Red (633nm)" package="5 mm [THT]"]
  R1 = Resistor [tolerance=±5% resistance=330 package=THT]
  R2 = Resistor [tolerance=±5% resistance=330 package=THT]
  J19 = female pin header, 2 pins [form="♀ (female)"]
  J20 = female pin header, 3 pins [form="♀ (female)"]
  J21 = female pin header, 1 pin [form="♀ (female)"]
  J23 = Camdenboss CTB0158-2 [part_number=CTB0158-2 package=THT]
  C1 = Electrolytic Capacitor [capacitance=1µF package="100 mil [THT, electrolytic]"]
  C2 = Electrolytic Capacitor [capacitance=1µF package="100 mil [THT, electrolytic]"]
  J1 = female pin header, 2 pins [form="♀ (female)"]
  J22 = female pin header, 2 pins [form="♀ (female)"]
  J6 = female pin header, 6 pins [form="♀ (female)"]
  J5 = female pin header, 7 pins [form="♀ (female)"]
  J18 = female pin header, 1 pin [form="♀ (female)"]
  J17 = female pin header, 1 pin [form="♀ (female)"]

nets:
  N1: Part1.A8, J7.pin1
  N2: Part1.A9, J7.pin2
  N3: Part1.A10, J7.pin3
  N4: Part1.A11, J7.pin4
  N5: Part1.A0, J6.pin1
  N6: Part1.A1, J6.pin2
  N7: Part1.A2, J6.pin3
  N8: Part1.A3, J6.pin4
  N9: Part1.A4, J6.pin5
  N10: Part1.A5, J6.pin6
  N11: Part1.D21/SCL, J1.pin2
  N12: Part1.D20/SDA, J1.pin1
  N13: Part1.D19/RX1, U8.D8, J22.pin2
  N14: Part1.D18/TX1, U8.D7, J22.pin1
  N15: Part1.D17_PWM/RX2, J5.pin2
  GND: Part1.GND, U8.GND, LED1.cathode, LED2.cathode, J23.pin1, C1.+, C2.-, J5.pin1, J17.pin1
  N16: Part1.D12_PWM, J5.pin3
  N17: Part1.D11_PWM, J5.pin4
  N18: Part1.D10_PWM, J5.pin5
  N19: Part1.D9_PWM, J5.pin6
  N20: Part1.D8_PWM, J5.pin7
  VIN: Part1.VIN, U8.Vin, J23.pin2, C1.-, C2.+
  N21: Part1.D2_PWM, U7.8
  N22: Part1.D3_PWM, U6.8
  N23: Part1.D4_PWM, U5.8
  N24: Part1.D5_PWM, U3.8
  N25: Part1.D6_PWM, U4.8
  N26: Part1.D7_PWM, U2.8
  N27: Part1.D22, U3.6
  N28: Part1.D23, U5.6
  N29: Part1.D24, U4.6
  N30: Part1.D25, U6.6
  N31: Part1.D26, U2.6
  N32: Part1.D27, U7.6
  N33: Part1.D29, J18.pin1
  N34: Part1.D30, U3.4
  N35: Part1.D31, U5.4
  N36: Part1.D32, U4.4
  N37: Part1.D33, U6.4
  N38: Part1.D34, U2.4
  N39: Part1.D35, U7.4
  N40: Part1.D36, J19.pin1
  N41: Part1.D38, J19.pin2
  N42: Part1.D40, U4.1
  N43: Part1.D41, U3.1
  N44: Part1.D42, U2.1
  N45: Part1.D43, U5.1
  N46: Part1.D44, J20.pin1
  N47: Part1.D45, U6.1
  N48: Part1.D46, J20.pin2
  N49: Part1.D47, U7.1
  N50: Part1.D48, J20.pin3
  N51: Part1.D49, J21.pin1
  N52: Part1.D50, U2.5, U3.5, U4.5, U5.5, U6.5, U7.5, J2.pin1
  N53: Part1.D51, U2.3, U3.3, U4.3, U5.3, U6.3, U7.3, J3.pin1
  N54: Part1.D52, U2.7, U3.7, U4.7, U5.7, U6.7, U7.7, J2.pin2
  N55: Part1.D53, J3.pin2
  N56: U8.D2, R2.Pin_0
  N57: U8.D3, R1.Pin_0
  N58: LED1.anode, R2.Pin_1
  N59: LED2.anode, R1.Pin_1

notes:
  Buzzer

custom parts:
  ESP8266 NodeMCU LoLin module: ESP8266 based NodeMCU
